// Logisim project 4bitALU.circ as structural Verilog: 6 circuits, main circuit main
module main (
  input  in_1,
  input  Input,
  input  in_3,
  input  in_4,
  input  in_5,
  input  Input_2,
  input  in_7,
  input  in_8,
  input  Control,
  input  in_10,
  output CarryOut,
  output out_12,
  output out_13,
  output out_14,
  output Output
);

  _4bitALU _4_bit_ALU (
    .CarryOut(CarryOut), .Control(Control), .Control_2(in_10), .A3(in_1), .A2(Input), .A1(in_3), .A0(in_4),
    .B3(in_5), .B2(Input_2), .B1(in_7), .B0(in_8), .out_12(out_12), .out_13(out_13), .out_14(out_14),
    .out_15(Output));
endmodule

module FullAdder (
  input  A,
  input  B,
  input  C,
  output SUM,
  output CARRY
);

  wire and_1_out, and_2_out, xor_1_out;

  xor xor_1 (xor_1_out, A, B);
  and and_1 (and_1_out, xor_1_out, C);
  and and_2 (and_2_out, A, B);
  xor xor_2 (SUM, xor_1_out, C);
  or or_1 (CARRY, and_1_out, and_2_out);
endmodule

module _1bitALU (
  input  Control,
  input  Control_2,
  input  CIN,
  input  A,
  input  B,
  output out_6,
  output COUT
);

  wire and_1_out, and_2_out, FullAdder_sum, n2linemultiplexer_1_out_4, not_1_out, or_1_out;

  not not_1 (not_1_out, B);
  _2lineMultiplexer u_2linemultiplexer_1 (.A(B), .B(not_1_out), .out_4(n2linemultiplexer_1_out_4), .CIN(and_2_out));
  and and_1 (and_1_out, A, B);
  or or_1 (or_1_out, B, A);
  FullAdder FullAdder (.A(CIN), .B(A), .C(n2linemultiplexer_1_out_4), .SUM(FullAdder_sum), .CARRY(COUT));
  and and_2 (and_2_out, Control, Control_2);
  _4lineMultiplexer u_4linemultiplexer_1 (
    .A(and_1_out), .B(or_1_out), .C(FullAdder_sum), .D(FullAdder_sum), .Control(Control),
    .Control_2(Control_2), .out_7(out_6));
endmodule

module _2lineMultiplexer (
  input  CIN,
  input  A,
  input  B,
  output out_4
);

  wire _0_out, _1_out, not_1_out;

  not not_1 (not_1_out, CIN);
  and _0 (_0_out, A, not_1_out);
  and _1 (_1_out, CIN, B);
  or or_1 (out_4, _0_out, _1_out);
endmodule

module _4lineMultiplexer (
  input  Control,
  input  Control_2,
  input  A,
  input  B,
  input  C,
  input  D,
  output out_7
);

  wire _00_out, _01_out, _10_out, _11_out, not_1_out, not_2_out, not_3_out, not_4_out;

  not not_1 (not_1_out, Control);
  not not_2 (not_2_out, Control_2);
  and _00 (_00_out, not_1_out, not_2_out, A);
  not not_3 (not_3_out, Control);
  and _01 (_01_out, not_3_out, Control_2, B);
  and _10 (_10_out, Control, not_4_out, C);
  not not_4 (not_4_out, Control_2);
  and _11 (_11_out, Control, Control_2, D);
  or or_1 (out_7, _00_out, _00_out, _01_out, _10_out, _11_out);
endmodule

module _4bitALU (
  input  A3,
  input  A2,
  input  A1,
  input  A0,
  input  B3,
  input  B2,
  input  B1,
  input  B0,
  input  Control,
  input  Control_2,
  output CarryOut,
  output out_12,
  output out_13,
  output out_14,
  output out_15
);

  wire _1_bit_ALU_2_cout, _1_bit_ALU_3_cout, _1_bit_ALU_4_cout, and_1_out;

  _1bitALU _1_bit_ALU (
    .A(A3), .B(B3), .out_6(out_12), .CIN(_1_bit_ALU_2_cout), .Control(Control), .Control_2(Control_2),
    .COUT(CarryOut));
  _1bitALU _1_bit_ALU_2 (
    .A(A2), .B(B2), .out_6(out_13), .CIN(_1_bit_ALU_3_cout), .Control(Control), .Control_2(Control_2),
    .COUT(_1_bit_ALU_2_cout));
  _1bitALU _1_bit_ALU_3 (
    .A(A1), .B(B1), .out_6(out_14), .CIN(_1_bit_ALU_4_cout), .Control(Control), .Control_2(Control_2),
    .COUT(_1_bit_ALU_3_cout));
  _1bitALU _1_bit_ALU_4 (
    .A(A0), .B(B0), .out_6(out_15), .CIN(and_1_out), .Control(Control), .Control_2(Control_2),
    .COUT(_1_bit_ALU_4_cout));
  and and_1 (and_1_out, Control, Control_2);
endmodule
